// Logisim project Alarme.circ as structural Verilog: 2 circuits, main circuit main
module main (
  input  LIGAR,
  input  SM
);

  wire and_1_out, and_2_out, and_3_out, and_4_out, and_5_out, and_6_out, clock_1_out, mostrador_1_a,
       mostrador_1_b, mostrador_1_c, mostrador_1_d, mostrador_1_e, mostrador_1_f, mostrador_1_g, not_1_out,
       or_1_out, or_2_out, t_ff_1_q, t_ff_1_qn, t_ff_2_q, t_ff_2_qn;

  Clock clock_1 (.out(clock_1_out));
  _7_Segment_Display u_7_segment_display_1 (
    .g(mostrador_1_g), .f(mostrador_1_f), .a(mostrador_1_a), .b(mostrador_1_b), .e(mostrador_1_e),
    .d(mostrador_1_d), .c(mostrador_1_c));  // open: dp
  T_Flip_Flop t_ff_1 (.clk(clock_1_out), .T(or_1_out), .Q(t_ff_1_q), .Qn(t_ff_1_qn));  // open: preset, reset, en
  T_Flip_Flop t_ff_2 (.clk(clock_1_out), .T(or_2_out), .Q(t_ff_2_q), .Qn(t_ff_2_qn));  // open: preset, reset, en
  mostrador mostrador_1 (
    .a(mostrador_1_a), .b(mostrador_1_b), .c(mostrador_1_c), .d(mostrador_1_d), .e(mostrador_1_e),
    .f(mostrador_1_f), .g(mostrador_1_g), .x1(t_ff_1_q), .x0(t_ff_2_q));
  not not_1 (not_1_out, LIGAR);
  and and_1 (and_1_out, LIGAR, t_ff_1_qn);
  and and_2 (and_2_out, not_1_out, t_ff_1_q);
  and and_3 (and_3_out, t_ff_1_q, SM, t_ff_2_qn);
  and and_4 (and_4_out, not_1_out, t_ff_2_q);
  and and_5 (and_5_out, t_ff_2_qn, t_ff_1_q, SM);
  or or_1 (or_1_out, and_1_out, and_2_out, and_3_out);
  or or_2 (or_2_out, and_4_out, and_5_out);
  and and_6 (and_6_out, t_ff_1_q, t_ff_2_q);
  LED led_1 (.in(and_6_out));

  // Notes on the sheet:
  //   T0
  //   T1
endmodule

module mostrador (
  input  x0,
  input  x1,
  output a,
  output b,
  output c,
  output d,
  output e,
  output f,
  output g
);

  or or_1 (a, x0, x1);
  and and_1 (b, x0, x1);
  and and_2 (c, x0, x1);
  or or_2 (d, x0, x1);
  and and_3 (e, x0, x1);
  and and_4 (f, x0, x1);

  assign g = 1'b1;
endmodule
